# Fritzing sketch LFR_Nano_L298N_MakerLine_Diagrams (saved by Fritzing 0.9.3b)

parts:
  M1 = Getriebemotor
  M2 = Getriebemotor
  BAT1 = BC9VPC [package=bc9vpc]
  ML1 = Maker Line
  Part1 = Arduino Nano (Rev3.0)
  L298N1 = L298N DC motor driver

nets:
  N1: M1.pin_1, L298N1.OUT3
  N2: M1.pin_2, L298N1.OUT4
  N3: M2.pin_1, L298N1.OUT1
  N4: M2.pin_2, L298N1.OUT2
  N5: BAT1.V+, L298N1.12V
  GND: BAT1.V-, ML1.GND, Part1.GND, L298N1.GND
  5V: ML1.VCC, Part1.5V, L298N1.5V
  N6: ML1.AN, Part1.A0
  N7: Part1.D5, L298N1.ENB
  N8: Part1.D6, L298N1.IN4
  N9: Part1.D7, L298N1.IN3
  N10: Part1.D8, L298N1.IN2
  N11: Part1.D9, L298N1.IN1
  N12: Part1.D10, L298N1.ENA

custom parts:
  Maker Line: Simplifying Line Sensor for Beginner.
  L298N DC motor driver: 2x DC motor driver with 78M05 positive voltage regulator (7..35 V) L298N: max 46 V, 2 A Set 5 V Enable jumper to enable 5 V regultor (needed for the L298N) and +5 V output at screw terminal or supply external +5 V at screw terminal Set ENA and/or ENB to +5 V to enable motor permanently or supply ENA and/or ENB with PWM signal IN1 and IN2 set rotation directory for motor A (OUT1/OUT2) IN2 and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
