# Fritzing sketch LFR_Nano_L298N_MakerLine_LCD_Diagrams (saved by Fritzing 0.9.3b)

parts:
  M1 = Getriebemotor
  M2 = Getriebemotor
  BAT1 = BC9VPC [package=bc9vpc]
  ML1 = Maker Line
  Part1 = Arduino Nano (Rev3.0)
  L298N1 = L298N DC motor driver
  U2 = POT [package=pot_alpha_rv16af-20]
  U3 = POT [package=pot_alpha_rv16af-20]
  Display1 = LCD screen 16x2 IIC [part_number=101290]

nets:
  N1: M1.pin_1, L298N1.OUT3
  N2: M1.pin_2, L298N1.OUT4
  N3: M2.pin_1, L298N1.OUT2
  N4: M2.pin_2, L298N1.OUT1
  N5: BAT1.V+, L298N1.12V
  GND: BAT1.V-, ML1.GND, Part1.GND, L298N1.GND, U2.A, U3.A, Display1.GND
  VCC: ML1.VCC, Part1.5V, L298N1.5V, U2.E, U3.E, Display1.VCC
  N6: ML1.AN, Part1.A0
  N7: Part1.D5, L298N1.ENB
  N8: Part1.D6, L298N1.IN4
  N9: Part1.D7, L298N1.IN3
  N10: Part1.D8, L298N1.IN2
  N11: Part1.D9, L298N1.IN1
  N12: Part1.D10, L298N1.ENA
  N13: Part1.A7, U3.S
  N14: Part1.A6, U2.S
  N15: Part1.A5, Display1.SCL
  N16: Part1.A4, Display1.SDA

notes:
  LineFollower Robot With Kp & Kd Tuning
  With Potentiometer and LCD

custom parts:
  Maker Line: Simplifying Line Sensor for Beginner.
  L298N DC motor driver: 2x DC motor driver with 78M05 positive voltage regulator (7..35 V) L298N: max 46 V, 2 A Set 5 V Enable jumper to enable 5 V regultor (needed for the L298N) and +5 V output at screw terminal or supply external +5 V at screw terminal Set ENA and/or ENB to +5 V to enable motor permanently or supply ENA and/or ENB with PWM signal IN1 and IN2 set rotation directory for motor A (OUT1/OUT2) IN2 and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
  LCD screen 16x2 IIC: LCD screen with HD44780 controller enables showing text, symbols, value or anything else that comes from Croduino/Arduino. It is capable of showing 16 symbols in two lines and therefore can be used in many projects that need to send clearly visible and legible output information.. • Color of symbols: White • Backlight: Blue • Dimensions: 80 x 36 x 12 mm • Screen dimensions: 64.5 x 16 mm •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

// code stored in the sketch: LFR_Nano_L298N_MakerLine_LCD_Code.ino

#include <LiquidCrystal_I2C.h> // Library for LCD
LiquidCrystal_I2C lcd = LiquidCrystal_I2C(0x27, 16, 2); // Change to (0x27,16,2) for 16x2 LCD.

#define MAKERLINE_AN  A0 // MAKERLINE AN pin ke A0 Nano

#define MAX_SPEED 150 // kalau ubah ni, kena ubah semula Kp dan Kd

//left wheel
int pwm1 = 10;
int in1 = 9;
int in2 = 8;
//right wheel
int pwm2 = 5;
int in3 = 7;
int in4 = 6;


//PID SETTING
float Kp = 0; //ubah
float Kd = 0; //ubah

//potentiomwter
int pinPP = A7;    //pin Analog 0 for the input of the potentiometer
int pinPD = A6;    //pin Analog 0 for the input of the potentiometer

int adcMakerLine = 0;
int adcSetPoint = 0;
int proportional = 0;
int lastProportional = 0;
int derivative = 0;
int powerDifference = 0;

int motorLeft = 0;
int motorRight = 0;

unsigned long currentMillis = 0;
unsigned long previousMillis = 0;
const int interval = 500;

void setup()
{
  pinMode(MAKERLINE_AN, INPUT);

  //potentiomwter
  pinMode (pinPP, INPUT);   //Pin Setup for potentiometer
  pinMode (pinPD, INPUT);   //Pin Setup for potentiometer

  //left wheel
  pinMode(pwm1, OUTPUT); //PWM-Pin
  pinMode(in1, OUTPUT); //IN1-Pin
  pinMode(in2, OUTPUT); //IN2-Pin
  //right wheel
  pinMode(pwm2, OUTPUT); //PWM-Pin
  pinMode(in3, OUTPUT); //IN1-Pin
  pinMode(in4, OUTPUT); //IN2-Pin

  Serial.begin(9600);
  Serial.println("PD Line Following Robot with Maker Line");
  lcd.init(); // initialize the lcd
  lcd.backlight();

  lcd.setCursor(0, 0);         // move cursor to   (0, 0)
  lcd.print("PD LFR by");        // print message at (0, 0)
  lcd.setCursor(2, 1);         // move cursor to   (2, 1)
  lcd.print("Sahrul Rashid"); // print message at (2, 1)
  // lcd.clear();

  // Place robot at the center of line
  adcSetPoint = analogRead(MAKERLINE_AN);
  delay(2000);
  lcd.clear();

}

void LCDRefresh() {

  currentMillis = millis();
  if (currentMillis - previousMillis > interval) {
    previousMillis = currentMillis;

    // Serial.print("Kd: ");
    // Serial.println(Kd);

    //  Serial.print("Kp: ");
    // Serial.print(Kp);

    // Serial.print("\t");

    //Serial.print("ADC:\t");
    // Serial.print(adcMakerLine);

    lcd.clear();
    lcd.setCursor(0, 0);
    lcd.print("Kp: ");
    lcd.print(Kp);
    lcd.setCursor(0, 1);
    lcd.print("Kd:  ");
    lcd.print(Kd);
  }
}

void loop() {

  LCDRefresh();

  Kp = analogRead(pinPP);
  Kp = Kp / 100;
  Kd = analogRead(pinPD);
  Kd = Kd / 50;



  //--------LFR--------------

  adcMakerLine = analogRead(MAKERLINE_AN);

  proportional = adcMakerLine - adcSetPoint;

  derivative = proportional - lastProportional;

  lastProportional = proportional;

  powerDifference = (proportional * Kp) + (derivative * Kd);


  motorLeft = MAX_SPEED + powerDifference;
  motorRight = MAX_SPEED - powerDifference;

  motorLeft = constrain(motorLeft, 0, MAX_SPEED);
  motorRight = constrain(motorRight, 0, MAX_SPEED);

  analogWrite(pwm1, motorLeft);
  digitalWrite(in1, HIGH);
  digitalWrite(in2, LOW);

  analogWrite(pwm2, motorRight);
  digitalWrite(in3, HIGH);
  digitalWrite(in4, LOW);

}
